# Fritzing sketch engineering-diagram (saved by Fritzing 1.0.8)
breadboards: 3

parts:
  S1 = Pushbutton [package="[THT]"]
  S2 = Pushbutton [package="[THT]"]
  S3 = Pushbutton [package="[THT]"]
  S4 = Pushbutton [package="[THT]"]
  S5 = Pushbutton [package="[THT]"]
  S6 = Pushbutton [package="[THT]"]
  S7 = Pushbutton [package="[THT]"]
  S8 = Pushbutton [package="[THT]"]
  Part2 = Arduino MKR1000
  BAT1 = Battery Holders [package=lipo-1100mAh]  # not connected
  LED1 = LED - 5mm [color="Yellow (595nm)" current=0.030A package="5 mm [THT]"]
  LED2 = LED - 5mm [color="Blue (430nm)" current=0.030A package="5 mm [THT]"]
  LED3 = LED - 5mm [color="Red (633nm)" current=0.030A package="5 mm [THT]"]
  LED4 = LED - 5mm [color="Green (555nm)" current=0.030A package="5 mm [THT]"]
  R1 = Resistor [tolerance=±5% power=0.25W resistance=220 package=THT]
  R2 = Resistor [tolerance=±5% power=0.25W resistance=220 package=THT]
  R3 = Resistor [tolerance=±5% power=0.25W resistance=220 package=THT]
  R4 = Resistor [tolerance=±5% power=0.25W resistance=220 package=THT]

nets:
  N1: S1.Pin_1, S1.Pin_2, S2.Pin_1, S2.Pin_2, S3.Pin_1, S3.Pin_2, S4.Pin_1, S4.Pin_2
  N2: S1.Pin_3, S1.Pin_4, Part2.D9_SCK
  N3: S2.Pin_3, S2.Pin_4, Part2.D8_MOSI
  N4: S3.Pin_3, S3.Pin_4, Part2.D6
  N5: S4.Pin_3, S4.Pin_4, Part2.D7
  N6: S5.Pin_1, S5.Pin_2, S6.Pin_1, S6.Pin_2, S7.Pin_1, S7.Pin_2, S8.Pin_1, S8.Pin_2
  N7: S5.Pin_3, S5.Pin_4, Part2.A1
  N8: S6.Pin_3, S6.Pin_4, Part2.A2
  N9: S7.Pin_3, S7.Pin_4, Part2.A3
  N10: S8.Pin_3, S8.Pin_4, Part2.A4
  N11: Part2.D2_PWM, LED4.anode
  N12: Part2.D3_PWM, LED3.anode
  N13: Part2.D4_PWM, LED2.anode
  N14: Part2.D5_PWM, LED1.anode
  N15: Part2.GND, R1.Pin_1, R2.Pin_1, R3.Pin_1, R4.Pin_1
  N16: LED1.cathode, R1.Pin_0
  N17: LED2.cathode, R2.Pin_0
  N18: LED3.cathode, R3.Pin_0
  N19: LED4.cathode, R4.Pin_0

custom parts:
  Arduino MKR1000: MKR1000 is a powerful board that combines the functionality of the Zero and the Wi-Fi Shield. It is the ideal solution for makers wanting to design IoT projects with minimal previous experience in networking
